// Logisim project control-logic.circ as structural Verilog: 1 circuit, main circuit control_logic
module control_logic (
  input  [31:0] inst,
  input  BrEq,
  input  BrLt,
  output PCSel,
  output RegWEn,
  output [2:0] ImmSel,
  output BrUn,
  output ASel,
  output BSel,
  output [3:0] ALUSel,
  output MemRW,
  output [1:0] WBSel,
  output CSRSel,
  output CSRWen
);

  wire B, decoder_1_out4, decoder_1_out28, I, J, O0, O5, O13, O25, or_6_out, or_7_out, R, U;
  wire [1:0] multiplexer_1_out;
  wire [3:0] multiplexer_3_out;
  wire [3:3] and_1_out;

  Decoder #(.enable("false"), .select(5)) decoder_1 (
    .out0(O0), .out4(decoder_1_out4), .out5(O5), .out8(MemRW), .out12(R), .out13(O13), .out24(B),
    .out25(O25), .out27(J), .out28(decoder_1_out28), .sel(inst[6:2]));  // open: out1, out2, out3, out6, out7, out9, out10, out11, out14, out15, out16, out17, out18, out19, out20, out21, out22, out23, out26, out29, out30, out31
  or or_1 (PCSel, O25, J, B, O5);
  or or_2 (RegWEn, R, I, J, U);
  or or_3 (I, O0, decoder_1_out4, O25, decoder_1_out28);
  or or_4 (U, O5, O13);
  or or_5 (ASel, O5, J, B);
  Priority_Encoder priority_encoder_1 (
    .in0(I), .in1(MemRW), .in2(B), .in3(U), .in4(J), .out(ImmSel));  // open: in5, in6, in7, en_in, gs, en_out
  and and_1 (and_1_out[3], inst[25], R);
  Multiplexer #(.enable("false"), .width(2)) multiplexer_1 (
    .in0(2'b01), .in1(2'b00), .out(multiplexer_1_out), .sel(O0));
  Multiplexer #(.enable("false"), .width(2)) multiplexer_2 (
    .in0(multiplexer_1_out), .in1(2'b10), .out(WBSel), .sel(or_6_out));
  or or_6 (or_6_out, O25, J);
  Multiplexer #(.enable("false"), .width(4)) multiplexer_3 (
    .in0({and_1_out[3], inst[14:12]}), .in1(4'b1111), .out(multiplexer_3_out), .sel(O13));
  Multiplexer #(.enable("false"), .width(4)) multiplexer_4 (
    .in0(multiplexer_3_out), .in1(4'b0000), .out(ALUSel), .sel(or_7_out));
  or or_7 (or_7_out, B, MemRW, O5, O25, O0, J);
  or or_8 (BSel, I, B, MemRW, U, J);

  assign BrUn = inst[13];

  // Other names for the same wires on the sheet: funct3[2:0] = inst[14:12]; opcode[6:0] = inst[6:0];
  //   funct7[6:0] = inst[31:25]; S = MemRW

  // Notes on the sheet:
  //   INPUTS to your circuit
  //   DON'T CHANGE THE LOCATIONS OF THE INPUTS AND OUTPUTS!
  //   OUTPUT from your circuit
endmodule
